# Fritzing sketch 001_FremdaLingva (saved by Fritzing 0.9.10b)
breadboards: 1

parts:
  Mod1 = Microbit
  LCD1 = LCD screen
  LCM1602_IIC1 = LCM1602 IIC [part_number="LCM1602 IIC" chip_label="LCM1602 IIC" package="DIP (Dual Inline) [THT]"]
  S1 = Round Pushbutton
  S2 = Round Pushbutton

nets:
  N1: Mod1.P1, S1.leg1
  N2: Mod1.P2, S2.leg1
  3V3: Mod1.3V3, Mod1.P19, LCM1602_IIC1.VCC, LCM1602_IIC1.SCL
  N3: Mod1.P20, LCM1602_IIC1.SDA
  GND: Mod1.GND, LCD1.VSS, LCM1602_IIC1.VSS, LCM1602_IIC1.GND, S1.leg0, S2.leg0
  VDD: LCD1.VDD, LCM1602_IIC1.VDD
  N4: LCD1.V0, LCM1602_IIC1.V0
  N5: LCD1.RS, LCM1602_IIC1.RS
  N6: LCD1.R/W, LCM1602_IIC1.RW
  N7: LCD1.E, LCM1602_IIC1.E
  N8: LCD1.DB0, LCM1602_IIC1.D0
  N9: LCD1.DB1, LCM1602_IIC1.D1
  N10: LCD1.DB2, LCM1602_IIC1.D2
  N11: LCD1.DB3, LCM1602_IIC1.D3
  N12: LCD1.DB4, LCM1602_IIC1.D4
  N13: LCD1.DB5, LCM1602_IIC1.D5
  N14: LCD1.DB6, LCM1602_IIC1.D6
  N15: LCD1.DB7, LCM1602_IIC1.D7
  N16: LCD1.LED+, LCM1602_IIC1.A
  N17: LCD1.LED-, LCM1602_IIC1.K

notes:
  P3
  P0
  P4
  P6
  P5
  P7
  P1
  P8
  P9
  P10
  P11
  P12
  P2
  P13
  P14
  P15
  P16
  3V3
  P19
  P20
  GND
  -
  Pin 6 set to high if solved

custom parts:
  Microbit: BBC Microbit Fritzing part. May 2019 expanded to include schematic and pcb views as well as breadboard. PCB view assumes an Adafruit PRODUCT ID: 3342 2x40 Right Angle through hole edge connector (although others will probably work as well). The pcb svg is custom (see forum article http://forum.fritzing.org/t/making-edge-connectors-and-both-side-smd-parts/7287 for an explaination if you need to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
  LCM1602 IIC: I2C-Module to use a 1602 or 2004 LCD on with the wire.h libory Serial LCD Modul
